# Fritzing sketch Kama_Joystick_Board_v2 (saved by Fritzing 0.9.3b)
circuit board: 2.8cm x 4.8cm
circuit board: 2.8cm x 4.9cm
breadboards: 1

parts:
  Joystick = Thumb Joystick [package=joystick]
  J1 = female pin header, 11 pins [form="♀ (female)"]  # not connected
  Pad198 = Pad [width=2 height=0.75 connect=center]
  Pad202 = Pad [width=2 height=0.75 connect=center]  # not connected
  Pad203 = Pad [width=2 height=0.75 connect=center]
  Pad205 = Pad [width=2 height=0.75 connect=center]
  Pad207 = Pad [width=2 height=0.75 connect=center]  # not connected
  Pad209 = Pad [width=2 height=0.75 connect=center]
  Pad210 = Pad [width=2 height=0.75 connect=center]
  Pad211 = Pad [width=2 height=0.75 connect=center]
  Pad212 = Pad [width=2 height=0.75 connect=center]
  Pad215 = Pad [width=2 height=0.75 connect=center]
  Pad220 = Pad [width=2 height=0.75 connect=center]
  Pad221 = Pad [width=2 height=0.75 connect=center]
  Pad224 = Pad [width=2 height=0.75 connect=center]
  Pad225 = Pad [width=2 height=0.75 connect=center]
  Pad227 = Pad [width=2 height=0.75 connect=center]
  Pad229 = Pad [width=2 height=0.75 connect=center]
  Pad231 = Pad [width=2 height=0.75 connect=center]
  Pad233 = Pad [width=2 height=0.75 connect=center]
  Pad241 = Pad [width=1 height=2.75 connect=center]
  Pad236 = Pad [width=1 height=2.75 connect=center]  # not connected
  Pad237 = Pad [width=1 height=2.75 connect=center]
  Pad238 = Pad [width=1 height=2.75 connect=center]
  Pad235 = Pad [width=1 height=2.75 connect=center]
  Pad234 = Pad [width=1 height=2.75 connect=center]
  Pad239 = Pad [width=1 height=2.75 connect=center]
  Pad240 = Pad [width=1 height=2.75 connect=center]
  Pad249 = Pad [width=1 height=2.75 connect=center]  # not connected
  Pad248 = Pad [width=1 height=2.75 connect=center]
  Pad247 = Pad [width=1 height=2.75 connect=center]  # not connected
  Pad246 = Pad [width=1 height=2.75 connect=center]  # not connected
  Pad245 = Pad [width=1 height=2.75 connect=center]
  Pad244 = Pad [width=1 height=2.75 connect=center]
  Pad243 = Pad [width=1 height=2.75 connect=center]  # not connected
  Pad242 = Pad [width=1 height=2.75 connect=center]  # not connected
  Qwiic = Qwiic JST [package=1x04-1mm-ra]
  GZC = Qwiic JST [package=1x04-1mm-ra]
  J3 = female pin header, 1 pin [form="♀ (female)"]  # not connected
  J5 = female pin header, 1 pin [form="♀ (female)"]  # not connected
  Joystick1 = Thumb Joystick [package=joystick]  # not connected
  Pad250 = Pad [width=1 height=2.75 connect=center]  # not connected
  Pad251 = Pad [width=1 height=2.75 connect=center]  # not connected
  Pad252 = Pad [width=1 height=2.75 connect=center]  # not connected
  Pad253 = Pad [width=1 height=2.75 connect=center]  # not connected
  Pad254 = Pad [width=1 height=2.75 connect=center]  # not connected
  Pad255 = Pad [width=1 height=2.75 connect=center]  # not connected
  Pad256 = Pad [width=1 height=2.75 connect=center]  # not connected
  Pad257 = Pad [width=1 height=2.75 connect=center]  # not connected
  Pad258 = Pad [width=1 height=2.75 connect=center]  # not connected
  Pad259 = Pad [width=1 height=2.75 connect=center]  # not connected
  Pad260 = Pad [width=1 height=2.75 connect=center]  # not connected
  Pad261 = Pad [width=1 height=2.75 connect=center]  # not connected
  Pad262 = Pad [width=1 height=2.75 connect=center]  # not connected
  Pad263 = Pad [width=1 height=2.75 connect=center]  # not connected
  Pad264 = Pad [width=1 height=2.75 connect=center]  # not connected
  Pad265 = Pad [width=1 height=2.75 connect=center]  # not connected
  SAMD21E18AF = TQFP32-5MM [chip_label=SAMD21E18AF package=TQFP]  # not connected

nets:
  N1: Joystick.SEL+, Pad220.pad
  N2: Joystick.V+, Joystick.H+, Qwiic.2
  N3: Joystick.SEL-, Joystick.H-, Joystick.V-, Pad198.pad, Pad224.pad, Pad241.pad, Pad240.pad, Pad248.pad, Qwiic.1, GZC.1, GZC.4
  N4: Joystick.V, Pad229.pad
  N5: Joystick.H, Pad225.pad
  N6: Pad203.pad, GZC.2
  N7: Pad205.pad, Pad239.pad
  N8: Pad209.pad, Pad244.pad
  N9: Pad210.pad, Pad235.pad
  N10: Pad211.pad, Pad234.pad
  N11: Pad212.pad, GZC.3
  N12: Pad215.pad, Qwiic.4
  N13: Pad221.pad, Qwiic.3
  N14: Pad227.pad, Pad245.pad
  N15: Pad231.pad, Pad238.pad
  N16: Pad233.pad, Pad237.pad

notes:
  ⟴ goo.gl/DttzBS
  SAMD21 15x15
  USB
  __
  _______
  GND
  SCL
  SDA
  D13
  D11
  D2
  PA13
  MISO
  SCK
  MOSI
  D3
  D4
  A0
  3v3
  A1
  D8
  RFM69HCW
  ANT
  CS
  RST
  IO5
  IO3
  IO4
  IRQ
  IO1
  IO2
  -
  +

custom parts:
  Qwiic JST: Header 4 Standard 4-pin 0.1 header. Use with straight break away headers (SKU : PRT-00116), right angle break away headers (PRT-00553), swiss pins (PRT-00743), machine pins (PRT-00117), and female headers (PRT-00115). Molex polarized connector foot print use with SKU : PRT-08231 with associated crimp pins and housings. 1MM SMD Version SKU: PRT-10208
