# Fritzing sketch Wii_Joystick_replacement (saved by Fritzing 0.9.3b)
circuit board: 2.3cm x 4.4cm
breadboards: 1

parts:
  J1 = male pin header, 3 pins [form="♂ (male)"]
  Part2 = Adafruit Feather M0 RFM69 [part_number="Adafruit #3176 or #3177"]  # not connected
  J3 = female pin header, 6 pins [form="♀ (female)"]
  J2 = female pin header, 9 pins [form="♀ (female)"]
  J4 = female pin header, 2 pins [form="♀ (female)"]
  Joystick = Thumb Joystick [package=joystick]
  Qwiic = Qwiic JST [package=1x04-1mm-ra]
  PWR = Header 2 [package=jst-2-smd]  # not connected

nets:
  N1: J1.pin1, J2.pin7, Joystick.SEL-, Joystick.H-, Joystick.V-, Qwiic.1
  N2: J1.pin2, J3.pin2
  N3: J1.pin3, J3.pin3
  N4: J3.pin1, Joystick.SEL+
  N5: J2.pin5, Joystick.V
  N6: J2.pin6, Joystick.H
  N7: J2.pin9, Joystick.V+, Joystick.H+, Qwiic.2
  N8: J4.pin1, Qwiic.3
  N9: J4.pin2, Qwiic.4

notes:
  V
  H
  ->
  G
  Z
  C
  Btn -
  Btn +
  V+
  V-
  Vs
  H-
  H+
  Hs
  Adafruit RFM69HCW
  M0 Feather
  HighJinx's
  NyKo Kama Wiichuk
  eMB Controller v1

custom parts:
  Adafruit Feather M0 RFM69: This is the Adafruit Feather M0 RFM69 Packet Radio - our take on an microcontroller with a RFM69HCW packet radio transceiver plus built in USB and battery charging. Its an Adafruit Feather M0 with a 433MHz or 900MHz radio module cooked in! We have other boards in the Feather family, check'em out here. At the Feather M0's heart is an ATSAMD21G18 ARM Cortex M0 processor, clocked at 48 MHz and at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
  Qwiic JST: Header 4 Standard 4-pin 0.1 header. Use with straight break away headers (SKU : PRT-00116), right angle break away headers (PRT-00553), swiss pins (PRT-00743), machine pins (PRT-00117), and female headers (PRT-00115). Molex polarized connector foot print use with SKU : PRT-08231 with associated crimp pins and housings. 1MM SMD Version SKU: PRT-10208
