# Fritzing sketch eMB_MetroM4_Sheild (saved by Fritzing 0.9.3b)
circuit board: 5.3cm x 5.3cm
breadboards: 1

parts:
  J3 = longpad pin header, 8 pins [form="long pad"]
  J4 = longpad pin header, 10 pins [form="long pad"]
  J1 = longpad pin header, 6 pins [form="long pad"]
  J2 = longpad pin header, 8 pins [form="long pad"]
  RFM1 = RFM69HCW ISM Transciever
  ESC = Qwiic JST [package=1x04-1mm-ra]
  Qwiic = Qwiic JST [package=1x04-1mm-ra]
  J5 = female pin header, 1 pin [form="♀ (female)"]
  Ant = SMA Antenna Connector [package=sma-edge]
  Attopilot = Qwiic JST [package=1x04-1mm-ra]
  Pad1 = Pad [width=4.0800000000000001 height=1.552212814814814 connect=center]
  10uF = Ceramic Capacitor [capacitance=10µF package="1206 [SMD, multilayer]"]
  ESP8266 = shrouded pin header, 8 pins [form="♂ (shrouded male)"]
  Pad2 = Pad [width=4.0800000000000001 height=1.552212814814814 connect=center]
  Pad3 = Pad [width=4.0800000000000001 height=1.552212814814814 connect=center]
  ICSP = double row female pin header, 6 pins [form="♀ (female)"]

nets:
  N1: J3.pin4, RFM1.6_RESET
  N2: J3.pin5, RFM1.14_DIO0
  N3: J3.pin7, ESC.3
  N4: J3.pin8, ESC.4
  N5: J4.pin1, Qwiic.4
  N6: J4.pin2, Qwiic.3
  N7: J4.pin4, Qwiic.1
  N8: J4.pin7, ESP8266.pin5
  N9: J4.pin8, ESP8266.pin1
  N10: J4.pin10, RFM1.5_NSS_(CS)
  N11: J1.pin1, Attopilot.3
  N12: J1.pin2, Attopilot.2
  N13: J2.pin4, RFM1.13_3.3V, Qwiic.2, 10uF.0, ESP8266.pin6, ESP8266.pin8
  N14: J2.pin6, ESC.1, Attopilot.1, ESP8266.pin4
  N15: J2.pin7, RFM1.1_GND
  N16: J2.pin8, ESC.2
  N17: RFM1.2_MISO, ICSP.pin1
  N18: RFM1.3_MOSI, ICSP.pin5
  N19: RFM1.4_SCK, ICSP.pin2
  N20: RFM1.8_GND, 10uF.1, Pad2.pad, Pad3.pad, ICSP.pin4
  N21: RFM1.9_ANT, J5.pin1, Ant.SIGNAL, Pad1.pad
  N22: RFM1.10_GND, Ant.GND

notes:
  VCC
  MOSI
  GND
  RST
  SCK
  MISO
  A0~
  A1~
  A2
  A3
  A4
  A5
  IOREF
  3v3
  5v
  VIN
  SCL
  SDA
  AREF
  ~13
  ~12
  ~11
  ~10
  ~9
  ~8
  ~7
  ~6
  ~5
  ~4
  ~3
  ~2
  Tx
  Rx
  IO0
  IO1
  CH_PD
  Rx>S2
  Tx<S2
  eMB MetroMx Shield v1
  A HighJinx Joint
  RFM69HCW Same Pinout
  as Adafruit RadioFruit
  RST - 4
  IRQ - 3
  CS  - 8

custom parts:
  RFM69HCW ISM Transciever: RF Transceiver by Hope RF. Well supported Arduino libraries are available. This ISM band transceiver is available in several frequencies e.g. 433MHz and 915MHz and it is also available in various feature versions.
  Qwiic JST: Header 4 Standard 4-pin 0.1 header. Use with straight break away headers (SKU : PRT-00116), right angle break away headers (PRT-00553), swiss pins (PRT-00743), machine pins (PRT-00117), and female headers (PRT-00115). Molex polarized connector foot print use with SKU : PRT-08231 with associated crimp pins and housings. 1MM SMD Version SKU: PRT-10208
