# Fritzing sketch eMB_MetroM4_Sheild_v6 (saved by Fritzing 0.9.3b)
circuit board: 5.3cm x 5.3cm
breadboards: 1

parts:
  J4 = longpad pin header, 10 pins [form="long pad"]
  J1 = longpad pin header, 6 pins [form="long pad"]
  J2 = longpad pin header, 8 pins [form="long pad"]
  ESC = Qwiic JST [package=1x04-1mm-ra]
  Qwiic = Qwiic JST [package=1x04-1mm-ra]
  J5 = female pin header, 1 pin [form="♀ (female)"]
  Ant = SMA Antenna Connector [package=sma-edge]
  Attopilot = Qwiic JST [package=1x04-1mm-ra]
  Pad1 = Pad [width=4.0800000000000001 height=1.552212814814814 connect=center]
  10uF = Ceramic Capacitor [capacitance=10µF package="1206 [SMD, multilayer]"]
  ESP-01 = shrouded pin header, 8 pins [form="♂ (shrouded male)"]
  Pad2 = Pad [width=4.0800000000000001 height=1.552212814814814 connect=center]
  Pad3 = Pad [width=4.0800000000000001 height=1.552212814814814 connect=center]
  ICSP = double row female pin header, 6 pins [form="♀ (female)"]
  Pad4 = Pad [width=1 height=2.75 connect=center]  # not connected
  Pad5 = Pad [width=1 height=2.75 connect=center]  # not connected
  Pad6 = Pad [width=1 height=2.75 connect=center]
  Pad7 = Pad [width=1 height=2.75 connect=center]
  Pad8 = Pad [width=1 height=2.75 connect=center]  # not connected
  Pad10 = Pad [width=1 height=2.75 connect=center]  # not connected
  Pad11 = Pad [width=1 height=2.75 connect=center]
  Pad12 = Pad [width=1 height=2.75 connect=center]
  Pad13 = Pad [width=1 height=2.75 connect=center]
  Pad14 = Pad [width=1 height=2.75 connect=center]
  Pad15 = Pad [width=1 height=2.75 connect=center]  # not connected
  Pad16 = Pad [width=1 height=2.75 connect=center]
  Pad17 = Pad [width=1 height=2.75 connect=center]
  Pad18 = Pad [width=1 height=2.75 connect=center]
  Pad19 = Pad [width=1 height=2.75 connect=center]
  Pad20 = Pad [width=1 height=2.75 connect=center]
  Pad46 = Pad [width=1.5 height=0.80000000000000004 connect=center]  # not connected
  Pad47 = Pad [width=1.5 height=0.80000000000000004 connect=center]
  Pad48 = Pad [width=1.5 height=0.80000000000000004 connect=center]
  Pad49 = Pad [width=1.5 height=0.80000000000000004 connect=center]
  Pad50 = Pad [width=1.5 height=0.80000000000000004 connect=center]  # not connected
  Pad51 = Pad [width=1.5 height=0.80000000000000004 connect=center]
  Pad52 = Pad [width=1.5 height=0.80000000000000004 connect=center]
  Pad53 = Pad [width=1.5 height=0.80000000000000004 connect=center]
  Pad54 = Pad [width=2 height=1.45 connect=center]  # not connected
  Pad55 = Pad [width=2 height=1.45 connect=center]  # not connected
  Pad56 = Pad [width=2 height=1.45 connect=center]  # not connected
  Pad57 = Pad [width=2 height=1.45 connect=center]  # not connected
  Pad82 = Pad [width=2.04 height=0.76000000000000001 connect=center]  # not connected
  Pad86 = Pad [width=2.04 height=0.76000000000000001 connect=center]  # not connected
  Pad85 = Pad [width=2.04 height=0.76000000000000001 connect=center]  # not connected
  Pad88 = Pad [width=2.04 height=0.76000000000000001 connect=center]  # not connected
  Pad89 = Pad [width=2.04 height=0.76000000000000001 connect=center]  # not connected
  Pad87 = Pad [width=2.04 height=0.76000000000000001 connect=center]  # not connected
  Pad83 = Pad [width=2.04 height=0.76000000000000001 connect=center]  # not connected
  Pad84 = Pad [width=2.04 height=0.76000000000000001 connect=center]  # not connected
  Pad106 = Pad [width=2.04 height=0.76000000000000001 connect=center]  # not connected
  Pad107 = Pad [width=2.04 height=0.76000000000000001 connect=center]  # not connected
  Pad108 = Pad [width=2.04 height=0.76000000000000001 connect=center]  # not connected
  Pad109 = Pad [width=2.04 height=0.76000000000000001 connect=center]  # not connected
  Pad110 = Pad [width=2.04 height=0.76000000000000001 connect=center]
  Pad111 = Pad [width=2.04 height=0.76000000000000001 connect=center]  # not connected
  Pad112 = Pad [width=2.04 height=0.76000000000000001 connect=center]  # not connected
  Pad113 = Pad [width=2.04 height=0.76000000000000001 connect=center]  # not connected
  Pad114 = Pad [width=2.04 height=0.76000000000000001 connect=center]  # not connected
  Pad115 = Pad [width=2.04 height=0.76000000000000001 connect=center]  # not connected
  Pad116 = Pad [width=2.04 height=0.76000000000000001 connect=center]  # not connected
  Pad117 = Pad [width=2.04 height=0.76000000000000001 connect=center]
  Pad118 = Pad [width=2.04 height=0.76000000000000001 connect=center]
  Pad119 = Pad [width=2.04 height=0.76000000000000001 connect=center]
  Pad120 = Pad [width=2.04 height=0.76000000000000001 connect=center]
  Pad121 = Pad [width=2.04 height=0.76000000000000001 connect=center]  # not connected
  J3 = longpad pin header, 8 pins [form="long pad"]

nets:
  N1: J4.pin1, Qwiic.4
  N2: J4.pin2, Qwiic.3
  N3: J4.pin4, Qwiic.1
  N4: J4.pin7, ESP-01.pin5, Pad119.pad
  N5: J4.pin8, ESP-01.pin1, Pad118.pad
  N6: J4.pin9, Pad49.pad
  N7: J4.pin10, Pad19.pad
  N8: J1.pin1, Attopilot.3
  N9: J1.pin2, Attopilot.2
  N10: J2.pin4, Qwiic.2, 10uF.0, ESP-01.pin6, ESP-01.pin8, Pad7.pad, Pad51.pad, Pad120.pad
  N11: J2.pin6, ESC.1, Attopilot.1, Attopilot.4, ESP-01.pin4, Pad110.pad, Pad117.pad
  N12: J2.pin7, Pad13.pad, Pad52.pad
  N13: J2.pin8, ESC.2
  N14: ESC.3, J3.pin7
  N15: ESC.4, J3.pin8
  N16: J5.pin1, Ant.SIGNAL, Pad1.pad, Pad12.pad
  N17: Ant.GND, Pad11.pad
  N18: 10uF.1, Pad2.pad, Pad3.pad, ICSP.pin4, Pad14.pad
  N19: ICSP.pin1, Pad18.pad, Pad53.pad
  N20: ICSP.pin2, Pad16.pad, Pad47.pad
  N21: ICSP.pin5, Pad17.pad, Pad48.pad
  N22: Pad6.pad, J3.pin5
  N23: Pad20.pad, J3.pin4

notes:
  VCC
  MOSI
  GND
  RST
  SCK
  MISO
  A0~
  A1~
  A2
  A3
  A4
  A5
  IOREF
  3v3
  5v
  VIN
  SCL
  SDA
  AREF
  ~13
  ~12
  ~11
  ~10
  ~9
  ~8
  ~7
  ~6
  ~5
  ~4
  ~3
  ~2
  Tx◂
  Rx▸
  Rx
  Tx
  IO0
  IO1
  CH_PD
  Rx▸S2
  Tx◂S2
  eMB MetroMx Shield v6
  A HighJinx Joint
  RFM69HCW Same Pinout
  as Adafruit RadioFruit:
  RST - 4
  IRQ - 3
  CS  - 8
  RFM69HCW
  ANT
  IO5
  CS
  IO3
  IO4
  IRQ
  I01
  I02
  N/C
  CS-D9
  MicroSD
  MicroSD Card:
  CS  - 9
  ITEAD PSF-A85
  ADC
  EN

custom parts:
  Qwiic JST: Header 4 Standard 4-pin 0.1 header. Use with straight break away headers (SKU : PRT-00116), right angle break away headers (PRT-00553), swiss pins (PRT-00743), machine pins (PRT-00117), and female headers (PRT-00115). Molex polarized connector foot print use with SKU : PRT-08231 with associated crimp pins and housings. 1MM SMD Version SKU: PRT-10208
