# Fritzing sketch eMB_Power_Conv_Board_v2 (saved by Fritzing 0.9.3b)
circuit board: 6cm x 3.00385cm
breadboards: 1

parts:
  USB-A = USB Connectors [package=usb-a-h]
  PWR_In = Screw terminal - 2 pins [package=THT]
  3v3_Out = Screw terminal - 2 pins [package=THT]
  In+ = female pin header, 1 pin [form="♀ (female)"]
  In- = female pin header, 1 pin [form="♀ (female)"]
  Out- = female pin header, 1 pin [form="♀ (female)"]
  Out+ = female pin header, 1 pin [form="♀ (female)"]
  PWR_In_2 = female pin header, 2 pins [form="♀ (female)"]
  PWR_Out = female pin header, 2 pins [form="♀ (female)"]
  J13 = female pin header, 2 pins [form="♀ (female)"]  # not connected

nets:
  N1: USB-A.VBUS, Out+.pin1, PWR_In_2.pin1
  N2: USB-A.GND, Out-.pin1, PWR_In_2.pin2
  N3: PWR_In.pin1, In-.pin1
  N4: PWR_In.pin2, In+.pin1
  N5: 3v3_Out.pin1, PWR_Out.pin2
  N6: 3v3_Out.pin2, PWR_Out.pin1

notes:
  ___________________
  ________
  -
  +
  ______________
  Fuzzy Noodle
  DC-DC Buck 3A
  goo.gl/eX3bcV
  LM2596 DC-DC
  4.5-40v Input
  1.3-35v 3A Output
  goo.gl/B7nnVY
  eMB Power Conversion Board
  A HighJinx Joint
  v2
