# Fritzing sketch eMB_SAMDx1_Sheild_v2 (saved by Fritzing 0.9.3b)
circuit board: 5.3cm x 5.3cm
breadboards: 1

parts:
  J4 = longpad pin header, 10 pins [form="long pad"]
  J1 = longpad pin header, 6 pins [form="long pad"]
  J2 = longpad pin header, 8 pins [form="long pad"]
  Qwiic = Qwiic JST [package=1x04-1mm-ra]
  J5 = female pin header, 1 pin [form="♀ (female)"]
  R_Ant = SMA Antenna Connector [package=sma-edge]
  Attopilot = Qwiic JST [package=1x04-1mm-ra]
  Pad1 = Pad [width=4.0800000000000001 height=1.552212814814814 connect=center]
  Pad2 = Pad [width=4.0800000000000001 height=1.552212814814814 connect=center]
  Pad3 = Pad [width=4.0800000000000001 height=1.552212814814814 connect=center]
  Pad4 = Pad [width=1 height=2.75 connect=center]  # not connected
  Pad5 = Pad [width=1 height=2.75 connect=center]  # not connected
  Pad6 = Pad [width=1 height=2.75 connect=center]
  Pad7 = Pad [width=1 height=2.75 connect=center]
  Pad8 = Pad [width=1 height=2.75 connect=center]  # not connected
  Pad10 = Pad [width=1 height=2.75 connect=center]  # not connected
  Pad11 = Pad [width=1 height=2.75 connect=center]
  Pad12 = Pad [width=1 height=2.75 connect=center]
  Pad13 = Pad [width=1 height=2.75 connect=center]
  Pad14 = Pad [width=1 height=2.75 connect=center]
  Pad15 = Pad [width=1 height=2.75 connect=center]  # not connected
  Pad16 = Pad [width=1 height=2.75 connect=center]
  Pad17 = Pad [width=1 height=2.75 connect=center]
  Pad18 = Pad [width=1 height=2.75 connect=center]
  Pad19 = Pad [width=1 height=2.75 connect=center]
  Pad20 = Pad [width=1 height=2.75 connect=center]
  Pad54 = Pad [width=2 height=1.45 connect=center]  # not connected
  Pad55 = Pad [width=2 height=1.45 connect=center]  # not connected
  Pad56 = Pad [width=2 height=1.45 connect=center]  # not connected
  Pad57 = Pad [width=2 height=1.45 connect=center]  # not connected
  Pad82 = Pad [width=2.04 height=0.76000000000000001 connect=center]  # not connected
  Pad86 = Pad [width=2.04 height=0.76000000000000001 connect=center]  # not connected
  Pad85 = Pad [width=2.04 height=0.76000000000000001 connect=center]  # not connected
  Pad88 = Pad [width=2.04 height=0.76000000000000001 connect=center]
  Pad89 = Pad [width=2.04 height=0.76000000000000001 connect=center]
  Pad87 = Pad [width=2.04 height=0.76000000000000001 connect=center]
  Pad83 = Pad [width=2.04 height=0.76000000000000001 connect=center]
  Pad84 = Pad [width=2.04 height=0.76000000000000001 connect=center]  # not connected
  Pad106 = Pad [width=2.04 height=0.76000000000000001 connect=center]  # not connected
  Pad107 = Pad [width=2.04 height=0.76000000000000001 connect=center]  # not connected
  Pad108 = Pad [width=2.04 height=0.76000000000000001 connect=center]  # not connected
  Pad109 = Pad [width=2.04 height=0.76000000000000001 connect=center]
  Pad110 = Pad [width=2.04 height=0.76000000000000001 connect=center]  # not connected
  Pad111 = Pad [width=2.04 height=0.76000000000000001 connect=center]  # not connected
  Pad112 = Pad [width=2.04 height=0.76000000000000001 connect=center]  # not connected
  Pad113 = Pad [width=2.04 height=0.76000000000000001 connect=center]  # not connected
  Pad114 = Pad [width=2.04 height=0.76000000000000001 connect=center]  # not connected
  Pad115 = Pad [width=2.04 height=0.76000000000000001 connect=center]  # not connected
  Pad116 = Pad [width=2.04 height=0.76000000000000001 connect=center]  # not connected
  Pad117 = Pad [width=2.04 height=0.76000000000000001 connect=center]  # not connected
  Pad118 = Pad [width=2.04 height=0.76000000000000001 connect=center]  # not connected
  Pad119 = Pad [width=2.04 height=0.76000000000000001 connect=center]
  Pad120 = Pad [width=2.04 height=0.76000000000000001 connect=center]  # not connected
  Pad121 = Pad [width=2.04 height=0.76000000000000001 connect=center]  # not connected
  J3 = longpad pin header, 8 pins [form="long pad"]
  10㎌ = Ceramic Capacitor [capacitance=10µF package="1206 [SMD, multilayer]"]
  ESC = Qwiic JST [package=1x04-1mm-ra]
  ESP-07/12 = ESP8266 WiFi Module [part_number=ESP8266]
  50k = Resistor [tolerance=±5% resistance=50k package="1206 [SMD]"]
  50k_2 = Resistor [tolerance=±5% resistance=50k package="1206 [SMD]"]
  50k_3 = Resistor [tolerance=±5% resistance=50k package="1206 [SMD]"]
  J15 = longpad pin header, 2 pins [form="long pad"]
  Pad122 = Pad [width=1.5 height=0.5 connect=center]
  Pad124 = Pad [width=1.5 height=0.5 connect=center]  # not connected
  Pad125 = Pad [width=1.5 height=0.5 connect=center]
  Pad126 = Pad [width=1.5 height=0.5 connect=center]  # not connected
  Pad127 = Pad [width=1.5 height=0.5 connect=center]
  Pad128 = Pad [width=1.5 height=0.5 connect=center]
  Pad129 = Pad [width=1.5 height=0.5 connect=center]
  Pad130 = Pad [width=1.5 height=0.5 connect=center]
  10㎌_2 = Ceramic Capacitor [capacitance=10µF package="1206 [SMD, multilayer]"]
  10㎌_3 = Ceramic Capacitor [capacitance=10µF package="1206 [SMD, multilayer]"]
  Pad131 = Pad [width=1.4278028404344232 height=2 connect=center]
  Pad132 = Pad [width=1.4278028404344232 height=2 connect=center]
  Pad133 = Pad [width=1.4278028404344232 height=2 connect=center]
  Pad134 = Pad [width=1.4278028404344232 height=2 connect=center]
  Pad135 = Pad [width=1.4278028404344232 height=2 connect=center]
  Pad136 = Pad [width=1.4278028404344232 height=2 connect=center]
  Pad137 = Pad [width=1.4278028404344232 height=2 connect=center]
  Pad138 = Pad [width=1.4278028404344232 height=2 connect=center]
  Pad139 = Pad [width=1.4278028404344232 height=2 connect=center]
  Pad140 = Pad [width=1.4278028404344232 height=2 connect=center]
  Pad141 = Pad [width=1.4278028404344232 height=2 connect=center]
  Pad142 = Pad [width=1.4278028404344232 height=2 connect=center]
  Pad143 = Pad [width=1.4278028404344232 height=2 connect=center]
  Pad144 = Pad [width=1.25 height=2.5 connect=center]
  Pad145 = Pad [width=1.25 height=2.5 connect=center]
  Pad146 = Pad [width=1.25 height=2.5 connect=center]
  ICSP = double row female pin header, 6 pins [form="♀ (female)"]
  ESP-01 = shrouded pin header, 8 pins [form="♂ (shrouded male)"]
  Rx▸ = Pad [width=1.5 height=1.5 connect=center]
  Tx◂ = Pad [width=1.5 height=1.5 connect=center]
  Pad149 = Pad [width=1.5 height=1.5 connect=center]
  Pad150 = Pad [width=1.5 height=1.5 connect=center]
  Tx◂_2 = Pad [width=1.5 height=1.5 connect=center]
  Rx▸_2 = Pad [width=1.5 height=1.5 connect=center]
  Tx◂_3 = Pad [width=1.5 height=1.5 connect=center]
  Rx▸_3 = Pad [width=1.5 height=1.5 connect=center]
  Pad151 = Pad [width=1.5 height=1.5 connect=center]
  Pad152 = Pad [width=1.5 height=1.5 connect=center]
  Pad153 = Pad [width=1.5 height=1.5 connect=center]
  Pad154 = Pad [width=1.5 height=1.5 connect=center]
  Pad155 = Pad [width=1.4278028404344232 height=2 connect=center]
  Pad156 = Pad [width=1.4278028404344232 height=2 connect=center]
  Pad157 = Pad [width=1.4278028404344232 height=2 connect=center]
  Pad158 = Pad [width=1.4278028404344232 height=2 connect=center]
  Pad159 = Pad [width=1.4278028404344232 height=2 connect=center]
  Pad160 = Pad [width=1.4278028404344232 height=2 connect=center]
  Pad161 = Pad [width=1.4278028404344232 height=2 connect=center]
  Pad162 = Pad [width=1.4278028404344232 height=2 connect=center]
  Pad163 = Pad [width=1.4278028404344232 height=2 connect=center]
  Pad164 = Pad [width=1.4278028404344232 height=2 connect=center]
  Pad165 = Pad [width=1.4278028404344232 height=2 connect=center]
  Pad166 = Pad [width=1.4278028404344232 height=2 connect=center]
  Pad167 = Pad [width=1.4278028404344232 height=2 connect=center]
  Pad168 = Pad [width=1.4278028404344232 height=2 connect=center]
  uFL = U.FL [package=u.fl]  # not connected
  Pad169 = Pad [width=1.4278028404344232 height=2 connect=center]
  Pad170 = Pad [width=1.4278028404344232 height=2 connect=center]
  Pad171 = Pad [width=1.4278028404344232 height=2 connect=center]
  Pad172 = Pad [width=1.4278028404344232 height=2 connect=center]
  GND = Pad [width=2.25 height=3.6375245925925896 connect=center]
  3v3 = Pad [width=2.25 height=3.6375245925925896 connect=center]
  J16 = female pin header, 2 pins [form="♀ (female)"]  # not connected
  Pad173 = Pad [width=1 height=0.80000000000000004 connect=center]
  Pad174 = Pad [width=1 height=0.80000000000000004 connect=center]
  Pad175 = Pad [width=1.5 height=1.5 connect=center]
  Pad176 = Pad [width=1.5 height=1.5 connect=center]
  Pad177 = Pad [width=1.5 height=1.5 connect=center]
  Pad178 = Pad [width=1.5 height=1.5 connect=center]
  J17 = Screw terminal - 2 pins [package=THT]  # not connected
  10㎌_4 = Ceramic Capacitor [capacitance=10µF package="1206 [SMD, multilayer]"]

nets:
  N1: J4.pin1, Qwiic.4, Pad143.pad
  N2: J4.pin2, Qwiic.3, Pad142.pad
  N3: J4.pin3, Pad141.pad
  N4: J4.pin4, Qwiic.1, Pad88.pad, Pad109.pad, ESP-07/12.GND, 10㎌_2.0, Pad155.pad, GND.pad
  N5: J4.pin5, Pad140.pad
  N6: J4.pin6, Pad139.pad
  N7: J4.pin7, Rx▸.pad, Pad172.pad
  N8: J4.pin8, Tx◂.pad, Pad171.pad
  N9: J4.pin9, 50k.Pin_1, Pad122.pad, Pad169.pad
  N10: J4.pin10, Pad19.pad, Pad170.pad
  N11: J1.pin1, Attopilot.3, Pad164.pad
  N12: J1.pin2, Attopilot.2, Pad163.pad
  N13: J1.pin3, Pad131.pad
  N14: J1.pin4, Pad132.pad
  N15: J1.pin5, Pad133.pad, Pad178.pad
  N16: J1.pin6, Pad134.pad, Pad177.pad
  N17: J2.pin2, Pad161.pad
  N18: J2.pin3, Pad160.pad
  N19: J2.pin4, Qwiic.2, Pad7.pad, 10㎌.1, 50k.Pin_0, 50k_2.Pin_0, 50k_3.Pin_0, Pad128.pad, 10㎌_2.1, ESP-01.pin6, ESP-01.pin8, Pad156.pad, 3v3.pad, 10㎌_4.0
  N20: J2.pin5, Pad157.pad
  N21: J2.pin6, Pad158.pad
  N22: J2.pin7, R_Ant.GND, Attopilot.1, Attopilot.4, Pad11.pad, Pad13.pad, ESC.1, 10㎌_3.0, ESP-01.pin4, Pad159.pad, 10㎌_4.1
  N23: J2.pin8, ESC.2, Pad162.pad
  N24: J5.pin1, R_Ant.SIGNAL, Pad1.pad, Pad12.pad
  N25: Pad2.pad, Pad3.pad, Pad14.pad, 10㎌.0, Pad125.pad, ICSP.pin4
  N26: Pad6.pad, J3.pin5, Pad167.pad
  N27: Pad16.pad, Pad129.pad, Pad144.pad, ICSP.pin2
  N28: Pad17.pad, 50k_2.Pin_1, Pad130.pad, Pad145.pad, ICSP.pin5
  N29: Pad18.pad, 50k_3.Pin_1, Pad127.pad, Pad146.pad, ICSP.pin1
  N30: Pad20.pad, J3.pin4, Pad168.pad
  N31: Pad89.pad, ESP-07/12.RXD, ESP-01.pin1, Pad150.pad, Pad151.pad, Pad176.pad
  N32: Pad87.pad, ESP-07/12.TXD, ESP-01.pin5, Pad149.pad, Pad152.pad, Pad175.pad
  N33: Pad83.pad, ESP-07/12.VCC, ESP-07/12.CH_PD, 10㎌_3.1, Pad173.pad
  N34: Pad119.pad, Pad174.pad
  N35: J3.pin1, Pad138.pad
  N36: J3.pin2, Pad137.pad
  N37: J3.pin3, Pad135.pad
  N38: J3.pin6, Pad136.pad
  N39: J3.pin7, Tx◂_2.pad, Pad153.pad, Pad165.pad
  N40: J3.pin8, Rx▸_2.pad, Pad154.pad, Pad166.pad
  N41: ESC.3, J15.pin1, Tx◂_3.pad
  N42: ESC.4, J15.pin2, Rx▸_3.pad

notes:
  VCC
  MOSI
  GND
  RST
  SCK
  MISO
  A0~
  A1~
  A2
  A3
  A4
  A5
  IOREF
  3v3
  5v
  VIN
  SCL
  SDA
  AREF
  ~13
  ~12
  ~11
  ~10
  ~9
  ~8
  ~7
  ~6
  ~5
  ~4
  ~3
  ~2
  Tx◂
  Rx▸
  Rx
  Tx
  IO0
  IO1
  CH_PD
  A HighJinx Joint
  RFM69HCW Same Pinout as
  Adafruit RadioFruit:
  RST - 4
  IRQ - 3
  CS  - 8
  RFM69HCW
  ANT
  IO5
  CS
  IO3
  IO4
  IRQ
  I01
  I02
  N/C
  CS-D9
  MicroSD
  MicroSD Card:
  CS  - 9
  ITEAD PSF-A85
  ADC
  EN
  Sf Serial1
  31/Rx▸
  30/Tx◂
  Shield v2θ
  eMB SAMDx1 Dev.
  Af Serial
  <(o.o<)
  ↑
  Serial2
  ↰
  ↱
  for Wifi
  for ESC
  Af SERCOM 1
  Sf Serial
  IORef
  ②
  ③
  ④
  ⑤
  ①
  ⓪
  ❷
  ❺
  ❻
  ❼
  ⓬
  ⓭
  Aref
  ❹
  ❸
  ❽
  ❾
  ❿
  ⓫
  3v3 PWR IN
  PSF En
  Af SERCOM 4
  Solder to
  ENABLE
  🃏

custom parts:
  Qwiic JST: Header 4 Standard 4-pin 0.1 header. Use with straight break away headers (SKU : PRT-00116), right angle break away headers (PRT-00553), swiss pins (PRT-00743), machine pins (PRT-00117), and female headers (PRT-00115). Molex polarized connector foot print use with SKU : PRT-08231 with associated crimp pins and housings. 1MM SMD Version SKU: PRT-10208
